# Fritzing sketch schematics (saved by Fritzing 1.0.4)
breadboards: 1

parts:
  Composant1 = Arduino Mega 2560 (Rev3)
  U1 = LCD-16X2 [package=lcd-16x2]  # not connected
  R1 = Trimmer Potentiometer [maximum_resistance=10kΩ knob_status=50% power=0.5W package=THT]
  R2 = Resistor [tolerance=±5% resistance=220 package="2512 [SMD]"]
  S1 = Pushbutton [package="[THT]"]
  R3 = Resistor [tolerance=±5% resistance=220 package="2512 [SMD]"]
  U2 = GAS_SENSOR [package=mq-3]
  J1 = Piezo Speaker
  T1 = TMP36 Temperature Sensor [thermistor_type=NTC package="TO92 [THT]"]  # not connected
  Composant2 = LED Matrix - Serial Interface - Red/Green/Blue
  Composant3 = LilyPad Accelerometer ADXL335

nets:
  N1: Composant1.D21/SCL, U2.A1
  N2: Composant1.D20/SDA, U2.B1
  N3: Composant1.GND, R1.leg2, S1.Pin_1, S1.Pin_2, U2.H2, J1.pin1, Composant3.YOUT
  N4: Composant1.D10_PWM, J1.pin2
  3V3: Composant1.3V3, Composant1.D22, Composant2.VCC
  N5: Composant1.5V, R1.leg1, R2.Pin_0, R3.Pin_0, U2.H1, Composant2.SCK, Composant3.XOUT
  N6: Composant1.D38, Composant3.ZOUT
  N7: Composant1.D40, S1.Pin_3, S1.Pin_4, R3.Pin_1

notes:
  SGP30 Mox gas sensor
  DHT 11 Temperature & Humidity sensor v2
  Motion sensor
